// Logisim project ThunderBoltv5.circ as structural Verilog: 12 circuits, main circuit COMPUTER
module COMPUTER (
);

  wire clock_module_1_clk, clock_module_1_sleeping, comparator_1_gt, comparator_1_lt, cpu_tb16_1_exception,
       cpu_tb16_1_hlt, cpu_tb16_1_io_we, cpu_tb16_1_mem_we, cpu_tb16_1_rst, cpu_tb16_1_timer_we,
       dipswitch_1_sw1, or_1_out;
  wire [15:0] cpu_tb16_1_address, cpu_tb16_1_d_in, cpu_tb16_1_io_tx, cpu_tb16_1_timer, dipswitch_2_sw16,
       io_driver_1_device_tx, io_driver_1_tx, ram64k_1_lsb, ram64k_1_msb;

  LED SLEEPING (.in(clock_module_1_sleeping));
  LED HALTED (.in(cpu_tb16_1_hlt));
  LED EXCEPTION (.in(cpu_tb16_1_exception));
  RAM64K ram64k_1 (
    .MSB(ram64k_1_msb), .LSB(ram64k_1_lsb), .ADDRESS(cpu_tb16_1_address), .CLK(clock_module_1_clk),
    .WE(cpu_tb16_1_mem_we), .D_IN(cpu_tb16_1_d_in));
  CPU_TB16 cpu_tb16_1 (
    .HLT(cpu_tb16_1_hlt), .RST(cpu_tb16_1_rst), .TIMER_WE(cpu_tb16_1_timer_we), .TIMER(cpu_tb16_1_timer),
    .IO_TX(cpu_tb16_1_io_tx), .IO_WE(cpu_tb16_1_io_we), .EXCEPTION(cpu_tb16_1_exception),
    .ADDRESS(cpu_tb16_1_address), .D_IN(cpu_tb16_1_d_in), .MEM_WE(cpu_tb16_1_mem_we),
    .CLK(clock_module_1_clk), .IO_RX(io_driver_1_tx), .MSB_IN(ram64k_1_msb), .LSB_IN(ram64k_1_lsb));  // open: IO_ADD, RX_SAKNOWLEDGE
  CLOCK_MODULE clock_module_1 (
    .sleeping(clock_module_1_sleeping), .CLK(clock_module_1_clk), .TIMER_LOAD(cpu_tb16_1_timer_we),
    .RST(cpu_tb16_1_rst), .TIME(cpu_tb16_1_timer), .HLT(cpu_tb16_1_hlt));
  IO_DRIVER io_driver_1 (
    .TX(io_driver_1_tx), .DEVICE_TX(io_driver_1_device_tx), .AVAILABLE(dipswitch_1_sw1),
    .WE(cpu_tb16_1_io_we), .DEVICE_RX(dipswitch_2_sw16), .RX(cpu_tb16_1_io_tx), .CLK(clock_module_1_clk),
    .RST(cpu_tb16_1_rst));
  LED Display_Refresh (.in(cpu_tb16_1_io_we));
  DipSwitch #(.number(2)) dipswitch_1 (.sw1(dipswitch_1_sw1));  // open: sw2
  Hex_Digit_Display hex_digit_display_1 (.value(io_driver_1_device_tx[15:12]));  // open: dp
  Hex_Digit_Display hex_digit_display_2 (.value(io_driver_1_device_tx[11:8]));  // open: dp
  Hex_Digit_Display hex_digit_display_3 ();  // open: value, dp
  Hex_Digit_Display hex_digit_display_4 ();  // open: value, dp
  // Binairy_to_BCD_converter #(.binvalue(13)) binairy_to_bcd_converter_1: pin names not known; wires that end beside it: io_driver_1_device_tx[12:0]
  or or_1 (or_1_out, comparator_1_gt, comparator_1_lt);
  Comparator #(.width(3)) comparator_1 (
    .a(io_driver_1_device_tx[15:13]), .b(3'b000), .gt(comparator_1_gt), .lt(comparator_1_lt));  // open: eq
  LED err (.in(or_1_out));
  DipSwitch #(.number(16)) dipswitch_2 (
    .sw1(dipswitch_2_sw16[15]), .sw2(dipswitch_2_sw16[14]), .sw3(dipswitch_2_sw16[13]),
    .sw4(dipswitch_2_sw16[12]), .sw5(dipswitch_2_sw16[11]), .sw6(dipswitch_2_sw16[10]),
    .sw7(dipswitch_2_sw16[9]), .sw8(dipswitch_2_sw16[8]), .sw9(dipswitch_2_sw16[7]),
    .sw10(dipswitch_2_sw16[6]), .sw11(dipswitch_2_sw16[5]), .sw12(dipswitch_2_sw16[4]),
    .sw13(dipswitch_2_sw16[3]), .sw14(dipswitch_2_sw16[2]), .sw15(dipswitch_2_sw16[1]),
    .sw16(dipswitch_2_sw16[0]));
  Hex_Digit_Display hex_digit_display_5 (.value(io_driver_1_device_tx[7:4]));  // open: dp
  Hex_Digit_Display hex_digit_display_6 (.value(io_driver_1_device_tx[3:0]));  // open: dp
  Hex_Digit_Display hex_digit_display_7 ();  // open: value, dp
  Hex_Digit_Display hex_digit_display_8 ();  // open: value, dp

  // Notes on the sheet:
  //   INPUT
  //   HEXADECIMAL DISPLAY
  //   DECIMAL DISPLAY
endmodule

module CPU_TB16 (
  input  [15:0] MSB_IN,
  input  [15:0] LSB_IN,
  input  [15:0] IO_RX,
  input  CLK,
  output TIMER_WE,
  output [15:0] TIMER,
  output [15:0] ADDRESS,
  output [15:0] D_IN,
  output MEM_WE,
  output [3:0] IO_ADD,
  output [15:0] IO_TX,
  output IO_WE,
  output RX_SAKNOWLEDGE,
  output RST,
  output EXCEPTION,
  output HLT
);

  wire ALU_F_EN, and_1_out, and_2_out, and_3_out, and_4_out, B_OPERAND_SEL, button_1_out, C, C_PASS, CLF,
       FLAG_EN, IR_LOAD, JMP_EN, LINK, MEM_DIN_SEL, or_5_out, or_6_out, PC_INC, PC_LOAD, PC_LOAD_SEL,
       PLA1_out, RF_WE, RST_t, TIMER_SEL;
  wire [1:0] ADD_SEL;
  wire [2:0] ir_1_out, ir_1_out_3, multiplexer_5_out, pull_resistor_11_node, RF_DIN_SEL;
  wire [2:2] ir_1_out_2;
  wire [3:0] alu_1_o, FLAG, FLAG_REG_q;
  wire [4:0] multiplexer_3_out, OPCODE;
  wire [15:0] ADD_IMM, adder_1_out, alu_1_out, multiplexer_1_out, multiplexer_6_out, multiplexer_9_out,
       pc_1_out, reg_file_1_rb;
  wire [31:8] pla_1_out;

  Pull_Resistor pull_resistor_1 (.node(PC_LOAD_SEL));
  Pull_Resistor pull_resistor_2 (.node(HLT));
  Multiplexer #(.enable("false"), .width(16)) multiplexer_1 (
    .in0(ADD_IMM), .in1(reg_file_1_rb), .out(multiplexer_1_out), .sel(PC_LOAD_SEL));
  or or_1 (RST, RST_t, button_1_out);
  Button button_1 (.out(button_1_out));
  LED CLOCK (.in(CLK));
  Pull_Resistor pull_resistor_3 (.node(PC_LOAD));
  Pull_Resistor pull_resistor_4 (.node(CLK));
  and and_1 (and_1_out, ~multiplexer_3_out[4], ~multiplexer_3_out[3], ~multiplexer_3_out[2], multiplexer_3_out[0]);  // AND_Gate
  or or_2 (ALU_F_EN, and_1_out, and_2_out, and_3_out);
  and and_2 (and_2_out, ~multiplexer_3_out[4], ~multiplexer_3_out[3], ~multiplexer_3_out[2], multiplexer_3_out[1]);  // AND_Gate
  and and_3 (and_3_out, ~multiplexer_3_out[4], multiplexer_3_out[3], multiplexer_3_out[2], ~multiplexer_3_out[1]);  // AND_Gate
  LED FETCH (.in(PC_INC));
  D_Flip_Flop d_ff_1 (.clk(CLK), .D(IR_LOAD), .Q(PC_INC), .Qn(IR_LOAD));  // open: preset, reset
  PC pc_1 (.OUT(pc_1_out), .PC_INC(PC_INC), .J_ADD(multiplexer_1_out), .PC_LOAD(PC_LOAD), .CLK(CLK), .RST(RST_t));
  LED EXECUTE (.in(IR_LOAD));
  Multiplexer #(.enable("false"), .select(2), .width(16)) multiplexer_2 (
    .in0(pc_1_out), .in1(ADD_IMM), .in2(reg_file_1_rb), .out(ADDRESS), .sel(ADD_SEL));  // open: in3
  Pull_Resistor pull_resistor_5 (.node(ADD_SEL));
  D_Flip_Flop d_ff_2 (.clk(CLK), .D(FLAG[0]), .Q(EXCEPTION));  // open: Qn, preset, reset
  Multiplexer #(.enable("false"), .width(5)) multiplexer_3 (
    .in0(OPCODE), .in1({5{1'b0}}), .out(multiplexer_3_out), .sel(IR_LOAD));
  PLA #(.in_width(5), .out_width(32), .\table ("00000 00000000000000000000000000000000 # NOP.\n00001 00000010000000000000000000000000 # RRRtype.\n00010 00000010000000000000000000000001 # RRItype.\n00011 00010010000000000000000000000000 # CarryOps chk\n00100 00000010000000000000000000010010 # LDR chk\n00101 00000100000000000000000000010000 # STR.\n00110 00000010000000000000000000100010 # LDRG.\n00111 00000100000000000000000000100000 # STRG.\n01000 00000010000000000000000000000100 # LDI.\n01001 00000010000000000000000000000110 # MOV.\n01010 00000000000000000000000000000000 # SVPC\n01010 00000000000000000000000000000000 # STPC\n01100 00100000000000000000000000000000 # CMP cjk\n01101 00100000000000000000000000000001 # CMI chk\n01110 00000000000000000000000000000000 # JMP\n01111 00001001000000000000000000000000 # RET.\n10000 00000000100000000000000000000000 # IOS.\n10001 00000010000000000000000000001010 # IOR\n10100 01000000000000000000000000000000 # CLF.\n11100 00000000001000000000000000000000 # RST\n11101 00000000010000000000000000000000 # SLP.\n11110 00000000010000000000000010000000 # SLR.\n11111 10000000000000000000000000000000 # HLT.")) pla_1 (
    .in(multiplexer_3_out),
    .out({pla_1_out[31], CLF, FLAG_EN, C_PASS, PC_LOAD_SEL, MEM_WE, RF_WE, pla_1_out[24], IO_WE, TIMER_WE, RST_t, pla_1_out[20:8], TIMER_SEL, MEM_DIN_SEL, ADD_SEL, RF_DIN_SEL, B_OPERAND_SEL}));
  and and_4 (and_4_out, ~multiplexer_3_out[4], multiplexer_3_out[3], multiplexer_3_out[2], multiplexer_3_out[1], ~multiplexer_3_out[0]);  // AND_Gate
  Multiplexer #(.enable("false"), .width(16)) multiplexer_4 (
    .in0(IO_TX), .in1(pc_1_out), .out(D_IN), .sel(MEM_DIN_SEL));
  Pull_Resistor pull_resistor_6 (.node(MEM_DIN_SEL));
  or or_3 (HLT, EXCEPTION, pla_1_out[31]);
  Pull_Resistor pull_resistor_7 (.node(MEM_WE));
  Adder #(.width(16)) adder_1 (.a(pc_1_out), .b(16'h2), .out(adder_1_out));  // open: cin, cout
  PLA #(.in_width(7), .out_width(1), .\table ("000xxxx 1 # UNCOND\n001x1xx 1 # EQ\n010x0xx 1 # NQ\n0111xxx 1 # LT\n1000xxx 1 # GT\n1011xxx 1 # LE\n101x1xx 1 # LE\n1100xxx 1 # GE\n110x1xx 1 # GE")) PLA1 (
    .in({IO_ADD[2:0], FLAG_REG_q}), .out(PLA1_out));
  and and_5 (LINK, IO_ADD[3], and_4_out, PLA1_out);
  and and_6 (JMP_EN, and_4_out, PLA1_out);
  IR ir_1 (
    .OUT({OPCODE, ir_1_out_3, ir_1_out, ir_1_out_2[2], ADD_IMM, IO_ADD}), .LSB_IN(LSB_IN), .MSB_IN(MSB_IN),
    .IR_LOAD(IR_LOAD), .CLK(CLK), .RST(RST_t));
  or or_4 (PC_LOAD, pla_1_out[24], JMP_EN);
  Pull_Resistor pull_resistor_8 (.node(FLAG_EN));
  Register #(.width(4)) FLAG_REG (.D(FLAG), .en(FLAG_EN), .Q(FLAG_REG_q), .clk(CLK), .clr(or_5_out));
  or or_5 (or_5_out, RST_t, CLF);
  Pull_Resistor pull_resistor_9 (.node(CLF));
  and and_7 (C, FLAG_REG_q[1], C_PASS);
  Pull_Resistor pull_resistor_10 (.node(C_PASS));
  Pull_Resistor pull_resistor_11 (.node(pull_resistor_11_node));
  Multiplexer #(.enable("false"), .width(3)) multiplexer_5 (
    .in0(ir_1_out_3), .in1(3'b110), .out(multiplexer_5_out), .sel(LINK));
  Multiplexer #(.enable("false"), .select(3), .width(16)) multiplexer_6 (
    .in0(alu_1_out), .in1(MSB_IN), .in2(ADD_IMM), .in3(IO_TX), .in4(adder_1_out), .in5(IO_RX),
    .out(multiplexer_6_out), .sel(pull_resistor_11_node));  // open: in6, in7
  Multiplexer #(.enable("false"), .width(3)) multiplexer_7 (
    .in0(RF_DIN_SEL), .in1(3'b100), .out(pull_resistor_11_node), .sel(LINK));
  or or_6 (or_6_out, LINK, RF_WE);
  Pull_Resistor pull_resistor_12 (.node(RF_WE));
  REG_FILE reg_file_1 (
    .Ra(IO_TX), .Rb(reg_file_1_rb), .WE(or_6_out), .Rb_sel(multiplexer_5_out), .D_IN(multiplexer_6_out),
    .CLK(CLK), .RST(RST_t), .Ra_sel(ir_1_out), .Rb_sel_2({ir_1_out_2[2], ADD_IMM[15:14]}));  // open: R0, R1, R2, R3, R4, R5_TR, R6_LR, R7_SP
  Multiplexer #(.enable("false"), .width(16)) multiplexer_8 (.in0(ADD_IMM), .in1(IO_TX), .out(TIMER), .sel(TIMER_SEL));
  Multiplexer #(.enable("false"), .width(16)) multiplexer_9 (
    .in0(reg_file_1_rb), .in1(ADD_IMM), .out(multiplexer_9_out), .sel(B_OPERAND_SEL));
  Pull_Resistor pull_resistor_13 (.node(B_OPERAND_SEL));
  ALU alu_1 (
    .O(alu_1_o[0]), .C(alu_1_o[1]), .OUT(alu_1_out), .Z(alu_1_o[2]), .S(alu_1_o[3]), .A(IO_TX),
    .B(multiplexer_9_out), .SEL(IO_ADD), .Cin(C));
  assign FLAG = ALU_F_EN ? alu_1_o : 4'bz;  // Controlled_Buffer controlled_buffer_1

  // Other names for the same wires on the sheet: OVERFLOW = FLAG[0]; ALUOP[3:0] = IO_ADD; COND[3:0] = IO_ADD;
  //   IO_PORT[3:0] = IO_ADD

  // Notes on the sheet:
  //   ENABLE ALUFLAGS only for opcode 123
  //   RAM
  //   szco
  //   CONTROL UNIT
  //   TIMER
  //   A-VALUE
  //   INPUT/OUTPUT
endmodule

module ALU (
  input  [15:0] A,
  input  [15:0] B,
  input  [3:0] SEL,
  input  Cin,
  output O,
  output Z,
  output S,
  output [15:0] OUT,
  output C
);

  wire adder_1_cout, and_2_out, and_4_out, and_5_out, and_6_out, nand_2_out, nor_2_out, nor_3_out, or_2_out,
       or_3_out, subtractor_1_bout;
  wire [15:0] adder_1_out, and_1_out, divider_1_out, divider_1_rem, multiplier_1_out, nand_1_out, nor_1_out,
       not_1_out, or_1_out, shifter_1_out, shifter_2_out, shifter_3_out, shifter_4_out, shifter_5_out,
       subtractor_1_out, xor_1_out;

  Pull_Resistor pull_resistor_1 (.node(Cin));
  assign not_1_out = ~A;  // NOT_Gate not_1, 16 bits wide
  assign and_1_out = A & B;  // AND_Gate and_1, 16 bits wide
  assign or_1_out = A | B;  // OR_Gate or_1, 16 bits wide
  assign nand_1_out = ~(A & B);  // NAND_Gate nand_1, 16 bits wide
  assign nor_1_out = ~(A | B);  // NOR_Gate nor_1, 16 bits wide
  assign xor_1_out = A ^ B;  // XOR_Gate xor_1, 16 bits wide
  Adder #(.width(16)) adder_1 (.a(A), .b(B), .out(adder_1_out), .cin(Cin), .cout(adder_1_cout));
  Subtractor #(.width(16)) subtractor_1 (.a(A), .b(B), .out(subtractor_1_out), .bin(Cin), .bout(subtractor_1_bout));
  Multiplier #(.mode("unsigned"), .width(16)) multiplier_1 (
    .a(A), .b(B), .out(multiplier_1_out), .cin({16{1'b0}}));  // open: cout
  Divider #(.width(16)) divider_1 (.a(A), .b(B), .out(divider_1_out), .rem(divider_1_rem));  // open: upper
  Shifter #(.width(16)) shifter_1 (.in(A), .\dist (B[3:0]), .out(shifter_1_out));
  Shifter #(.shift("lr"), .width(16)) shifter_2 (.in(A), .\dist (B[3:0]), .out(shifter_2_out));
  Shifter #(.shift("ar"), .width(16)) shifter_3 (.in(A), .\dist (B[3:0]), .out(shifter_3_out));
  Shifter #(.shift("rl"), .width(16)) shifter_4 (.in(A), .\dist (B[3:0]), .out(shifter_4_out));
  Shifter #(.shift("rr"), .width(16)) shifter_5 (.in(A), .\dist (B[3:0]), .out(shifter_5_out));
  nor nor_2 (nor_2_out, B[15], A[15]);
  and and_2 (and_2_out, nor_2_out, OUT[15]);
  nor nor_3 (nor_3_out, OUT[15], nand_2_out);
  nand nand_2 (nand_2_out, B[15], A[15]);
  or or_2 (or_2_out, and_2_out, nor_3_out);
  and and_3 (O, or_2_out, or_3_out);
  Multiplexer #(.enable("false"), .select(4), .width(16)) multiplexer_1 (
    .in0(not_1_out), .in1(and_1_out), .in2(or_1_out), .in3(nand_1_out), .in4(nor_1_out), .in5(xor_1_out),
    .in6(adder_1_out), .in7(subtractor_1_out), .in8(multiplier_1_out), .in9(divider_1_out),
    .in10(divider_1_rem), .in11(shifter_1_out), .in12(shifter_2_out), .in13(shifter_3_out),
    .in14(shifter_4_out), .in15(shifter_5_out), .out(OUT), .sel(SEL));
  and and_4 (and_4_out, SEL[3], ~SEL[2], ~SEL[1], SEL[0]);  // AND_Gate
  and and_5 (and_5_out, ~SEL[3], SEL[2], SEL[1], ~SEL[0]);  // AND_Gate
  Multiplexer #(.enable("false")) multiplexer_2 (.in0(adder_1_cout), .in1(subtractor_1_bout), .out(C), .sel(and_4_out));
  or or_3 (or_3_out, and_5_out, and_6_out);
  and and_6 (and_6_out, SEL[3], ~SEL[2], ~SEL[1], ~SEL[0]);  // AND_Gate
  nor nor_4 (Z, OUT[0], OUT[1], OUT[2], OUT[3], OUT[4], OUT[5], OUT[6], OUT[7], OUT[8], OUT[9], OUT[10], OUT[11], OUT[12], OUT[13], OUT[14], OUT[15]);

  assign S = OUT[15];

  // Notes on the sheet:
  //   16-Bit Arithmetic and Logic unit
  //   rotate
  //   logical shift L&R
  //   0:not
  //   1:and
  //   2:or
  //   3:nand
  //   4:nor
  //   5:xor
  //   6:add
  //   7:sub
  //   8:mul
  //   9:div
  //   10:rem
  //   11:lsl
  //   12:lsr
  //   13:asr
  //   14:rol
  //   15:ror
  //   flag outputs:
  //   S: sign flag
  //   Z: zero flag
  //   C: carry flag
  //   O: overfow flag
  //   TO ENSURE OVERFLOW ONLY IN ADD SUB AND MUL
endmodule

module REG (
  input  [15:0] IN,
  input  IN1,
  input  CLK,
  input  RST,
  output [15:0] OUT
);

  Register #(.width(16)) register_1 (.D(IN), .en(IN1), .Q(OUT), .clk(CLK), .clr(RST));
endmodule

module REG_FILE (
  input  CLK,
  input  RST,
  input  [15:0] D_IN,
  input  WE,
  input  [2:0] Ra_sel,
  input  [2:0] Rb_sel,
  input  [2:0] Rb_sel_2,
  output [15:0] Ra,
  output [15:0] Rb,
  output [15:0] R0,
  output [15:0] R1,
  output [15:0] R2,
  output [15:0] R3,
  output [15:0] R4,
  output [15:0] R5_TR,
  output [15:0] R6_LR,
  output [15:0] R7_SP
);

  wire demultiplexer_1_out0, demultiplexer_1_out1, demultiplexer_1_out2, demultiplexer_1_out3,
       demultiplexer_1_out4, demultiplexer_1_out5, demultiplexer_1_out6, demultiplexer_1_out7;

  Demultiplexer #(.enable("false"), .select(3)) demultiplexer_1 (
    .out0(demultiplexer_1_out0), .out1(demultiplexer_1_out1), .out2(demultiplexer_1_out2),
    .out3(demultiplexer_1_out3), .out4(demultiplexer_1_out4), .out5(demultiplexer_1_out5),
    .out6(demultiplexer_1_out6), .out7(demultiplexer_1_out7), .in(WE), .sel(Rb_sel));
  REG reg_1 (.OUT(R0), .IN(D_IN), .IN1(demultiplexer_1_out0), .CLK(CLK), .RST(RST));
  REG reg_2 (.OUT(R1), .IN(D_IN), .IN1(demultiplexer_1_out1), .CLK(CLK), .RST(RST));
  REG reg_3 (.OUT(R2), .IN(D_IN), .IN1(demultiplexer_1_out2), .CLK(CLK), .RST(RST));
  REG reg_4 (.OUT(R3), .IN(D_IN), .IN1(demultiplexer_1_out3), .CLK(CLK), .RST(RST));
  REG reg_5 (.OUT(R4), .IN(D_IN), .IN1(demultiplexer_1_out4), .CLK(CLK), .RST(RST));
  REG reg_6 (.OUT(R5_TR), .IN(D_IN), .IN1(demultiplexer_1_out5), .CLK(CLK), .RST(RST));
  REG reg_7 (.OUT(R6_LR), .IN(D_IN), .IN1(demultiplexer_1_out6), .CLK(CLK), .RST(RST));
  REG reg_8 (.OUT(R7_SP), .IN(D_IN), .IN1(demultiplexer_1_out7), .CLK(CLK), .RST(RST));
  Multiplexer #(.enable("false"), .select(3), .width(16)) multiplexer_1 (
    .in0(R0), .in1(R1), .in2(R2), .in3(R3), .in4(R4), .in5(R5_TR), .in6(R6_LR), .in7(R7_SP), .out(Ra),
    .sel(Ra_sel));
  Multiplexer #(.enable("false"), .select(3), .width(16)) multiplexer_2 (
    .in0(R0), .in1(R1), .in2(R2), .in3(R3), .in4(R4), .in5(R5_TR), .in6(R6_LR), .in7(R7_SP), .out(Rb),
    .sel(Rb_sel_2));
endmodule

module PC (
  input  PC_INC,
  input  PC_LOAD,
  input  CLK,
  input  RST,
  input  [15:0] J_ADD,
  output [15:0] OUT
);

  wire [15:0] adder_1_out, multiplexer_1_out, multiplexer_2_out;

  Adder #(.width(16)) adder_1 (.a(OUT), .b(16'h2), .out(adder_1_out));  // open: cin, cout
  Multiplexer #(.enable("false"), .width(16)) multiplexer_1 (
    .in0(OUT), .in1(adder_1_out), .out(multiplexer_1_out), .sel(PC_INC));
  Multiplexer #(.enable("false"), .width(16)) multiplexer_2 (
    .in0(multiplexer_1_out), .in1(J_ADD), .out(multiplexer_2_out), .sel(PC_LOAD));
  REG reg_1 (.OUT(OUT), .IN(multiplexer_2_out), .IN1(1'b1), .CLK(CLK), .RST(RST));
endmodule

module IR (
  input  [15:0] LSB_IN,
  input  IR_LOAD,
  input  [15:0] MSB_IN,
  input  CLK,
  input  RST,
  output [31:0] OUT
);

  Register #(.width(32)) register_1 (.D({MSB_IN, LSB_IN}), .en(IR_LOAD), .Q(OUT), .clk(CLK), .clr(RST));
endmodule

module RAM64K (
  input  WE,
  input  [15:0] ADDRESS,
  input  CLK,
  input  [15:0] D_IN,
  output [15:0] MSB,
  output [15:0] LSB
);

  wire comparator_1_eq, demultiplexer_1_out0, demultiplexer_1_out1, not_1_out, not_2_out;
  wire [15:0] divider_1_rem, multiplexer_1_out, ram_1_p8, ram_1_p9, subtractor_1_out;

  Divider #(.width(16)) divider_1 (.a(ADDRESS), .b(16'h2), .rem(divider_1_rem));  // open: out, upper
  Subtractor #(.width(16)) subtractor_1 (
    .a(ADDRESS), .b({16{1'b0}}), .out(subtractor_1_out), .bin(1'b1));  // open: bout
  Comparator #(.width(16)) comparator_1 (.a(divider_1_rem), .b({16{1'b0}}), .eq(comparator_1_eq));  // open: gt, lt
  Multiplexer #(.enable("false"), .width(16)) multiplexer_1 (
    .in0(subtractor_1_out), .in1(ADDRESS), .out(multiplexer_1_out), .sel(comparator_1_eq));
  Demultiplexer #(.enable("false")) demultiplexer_1 (
    .out0(demultiplexer_1_out0), .out1(demultiplexer_1_out1), .in(1'b1), .sel(not_1_out));
  not not_1 (not_1_out, comparator_1_eq);
  // RAM #(.addrWidth(16), .dataWidth(16), .line("dual"), .\type ("nonvolatile")) ram_1: pin names not known; wires that end beside it: multiplexer_1_out, WE, demultiplexer_1_out0, demultiplexer_1_out1, CLK, D_IN, D_IN, ram_1_p8, ram_1_p9
  not not_2 (not_2_out, comparator_1_eq);
  Multiplexer #(.enable("false"), .width(16)) multiplexer_2 (
    .in0(ram_1_p8), .in1(ram_1_p9), .out(MSB), .sel(not_2_out));
  assign LSB = comparator_1_eq ? ram_1_p9 : 16'bz;  // Controlled_Buffer controlled_buffer_1
endmodule

module CLOCK_MODULE (
  input  HLT,
  input  TIMER_LOAD,
  input  [15:0] TIME,
  input  RST,
  output CLK,
  output sleeping
);

  wire and_1_out, clock_1_out, comparator_1_eq;
  wire [15:0] counter_1_q;

  Clock clock_1 (.out(clock_1_out));
  and and_1 (and_1_out, clock_1_out, ~HLT);  // AND_Gate
  Counter #(.max('hffff), .width(16)) counter_1 (
    .load(TIMER_LOAD), .D(TIME), .count(sleeping), .Q(counter_1_q), .up(1'b0), .clk(and_1_out), .clr(RST));  // open: carry
  not not_1 (sleeping, comparator_1_eq);
  LED u_CLK (.in(and_1_out));
  Comparator #(.width(16)) comparator_1 (.a(counter_1_q), .b({16{1'b0}}), .eq(comparator_1_eq));  // open: gt, lt
  and and_2 (CLK, and_1_out, comparator_1_eq);
endmodule

module IO_DRIVER (
  input  [15:0] DEVICE_RX,
  input  AVAILABLE,
  input  [15:0] RX,
  input  WE,
  input  CLK,
  input  RST,
  output [15:0] TX,
  output [15:0] DEVICE_TX
);

  REG reg_1 (.OUT(TX), .IN(DEVICE_RX), .IN1(AVAILABLE), .CLK(CLK), .RST(RST));
  REG reg_2 (.OUT(DEVICE_TX), .IN(RX), .IN1(WE), .CLK(CLK), .RST(RST));
endmodule

module IO_CONTROLLER (
  input  CLK,
  input  RST,
  input  WE,
  input  [1:0] ADD,
  input  [15:0] TX,
  output [15:0] RX,
  output alu_op
);

  wire demultiplexer_1_out0, demultiplexer_1_out1, demultiplexer_1_out2, demultiplexer_1_out3;
  wire [15:0] io_driver_1_tx, io_driver_2_tx, io_driver_3_tx, io_driver_4_tx;

  Demultiplexer #(.enable("false"), .select(2)) demultiplexer_1 (
    .out0(demultiplexer_1_out0), .out1(demultiplexer_1_out1), .out2(demultiplexer_1_out2),
    .out3(demultiplexer_1_out3), .in(WE), .sel(ADD));
  Multiplexer #(.enable("false"), .select(2), .width(16)) multiplexer_1 (
    .in0(io_driver_1_tx), .in1(io_driver_2_tx), .in2(io_driver_3_tx), .in3(io_driver_4_tx), .out(TX),
    .sel(ADD));
  IO_DRIVER io_driver_1 (
    .TX(io_driver_1_tx), .WE(demultiplexer_1_out0), .RX(RX), .CLK(CLK), .RST(RST));  // open: DEVICE_TX, AVAILABLE, DEVICE_RX
  IO_DRIVER io_driver_2 (
    .TX(io_driver_2_tx), .WE(demultiplexer_1_out1), .RX(RX), .CLK(CLK), .RST(RST));  // open: DEVICE_TX, AVAILABLE, DEVICE_RX
  IO_DRIVER io_driver_3 (
    .TX(io_driver_3_tx), .WE(demultiplexer_1_out2), .RX(RX), .CLK(CLK), .RST(RST));  // open: DEVICE_TX, AVAILABLE, DEVICE_RX
  IO_DRIVER io_driver_4 (
    .TX(io_driver_4_tx), .WE(demultiplexer_1_out3), .RX(RX), .CLK(CLK), .RST(RST));  // open: DEVICE_TX, AVAILABLE, DEVICE_RX
endmodule

module INTERRUPT_CONTROLLER (
  input  [15:0] IRQ,
  input  [7:0] Mask,
  input  Enable,
  input  Disable,
  input  clk
);

  wire [7:0] and_1_out;
  wire [7:7] s_r_ff_1_q;

  S_R_Flip_Flop s_r_ff_1 (.S(Enable), .clk(clk), .R(Disable), .Q(s_r_ff_1_q[7]));  // open: Qn, preset, reset
  assign and_1_out = IRQ[7:0] & Mask & {8{s_r_ff_1_q[7]}};  // AND_Gate and_1, 8 bits wide
  Register #(.width(12)) register_1 (.D({IRQ[11:8], and_1_out}), .clk(clk));  // open: en, Q, clr
  LED FETCH ();  // open: in
endmodule
